// Logisim project computer.circ as structural Verilog: 5 circuits, main circuit main
module main (
);

  wire alu_1_out_5, alu_1_out_8, \alu_1_结果为0信号 , CLK, \controller_1_alu减法 , \controller_1_alu加法 ,
       \controller_1_使能a寄存器 , \controller_1_使能b寄存器 , \controller_1_使能c寄存器 , \controller_1_使能d寄存器 ,
       \controller_1_节拍0 , \controller_1_节拍1 , \controller_1_节拍2 , \controller_1_节拍3 , \controller_1_节拍4 ,
       \controller_1_节拍5 , RST;
  wire [7:0] \alu_1_输出信号 , \controller_1_alu操作数a , \controller_1_alu操作数b , controller_1_ir, controller_1_pc,
       \controller_1_ram地址总线 , ram_1_data, \寄存器_A_q , \寄存器_B_q , \寄存器_C_q , \寄存器_D_q ;

  // Probe on \controller_1_alu加法 
  // Probe on \controller_1_alu减法 
  ALU alu_1 (
    .\操作数A (\controller_1_alu操作数a ), .\操作数B (\controller_1_alu操作数b ), .\加法 (\controller_1_alu加法 ),
    .\减法 (\controller_1_alu减法 ), .out_5(alu_1_out_5), .\输出信号 (\alu_1_输出信号 ), .\结果为0信号 (\alu_1_结果为0信号 ),
    .out_8(alu_1_out_8));
  // Probe on \controller_1_alu操作数a 
  // Probe on \controller_1_alu操作数b 
  // Probe on \alu_1_输出信号 
  Clock \u_时钟信号  (.out(CLK));
  Register \u_寄存器_A  (.D(ram_1_data), .en(\controller_1_使能a寄存器 ), .Q(\寄存器_A_q ), .clk(CLK), .clr(RST));
  Button \u_复位  (.out(RST));
  Controller controller_1 (
    .\时钟 (CLK), .\复位 (RST), .\RAM数据总线 (ram_1_data), .\RAM地址总线 (\controller_1_ram地址总线 ),
    .\使能A寄存器 (\controller_1_使能a寄存器 ), .\使能B寄存器 (\controller_1_使能b寄存器 ), .\使能C寄存器 (\controller_1_使能c寄存器 ),
    .\使能D寄存器 (\controller_1_使能d寄存器 ), .\ALU操作数A (\controller_1_alu操作数a ), .\ALU操作数B (\controller_1_alu操作数b ),
    .\ALU溢出 (alu_1_out_5), .\ALU为0 (\alu_1_结果为0信号 ), .\ALU为负 (alu_1_out_8), .\节拍0 (\controller_1_节拍0 ),
    .\节拍1 (\controller_1_节拍1 ), .\节拍2 (\controller_1_节拍2 ), .\节拍3 (\controller_1_节拍3 ),
    .\节拍4 (\controller_1_节拍4 ), .\节拍5 (\controller_1_节拍5 ), .PC(controller_1_pc), .IR(controller_1_ir),
    .\ALU加法 (\controller_1_alu加法 ), .\ALU减法 (\controller_1_alu减法 ), .\ALU结果 (\alu_1_输出信号 ),
    .\寄存器A (\寄存器_A_q ), .\寄存器B (\寄存器_B_q ), .\寄存器C (\寄存器_C_q ), .\寄存器D (\寄存器_D_q ));
  Register \u_寄存器_B  (.D(ram_1_data), .en(\controller_1_使能b寄存器 ), .Q(\寄存器_B_q ), .clk(CLK), .clr(RST));
  Register \u_寄存器_C  (.D(ram_1_data), .en(\controller_1_使能c寄存器 ), .Q(\寄存器_C_q ), .clk(CLK), .clr(RST));
  LED led_1 (.in(\controller_1_节拍0 ));
  LED led_2 (.in(\controller_1_节拍2 ));
  LED led_3 (.in(\controller_1_节拍3 ));
  LED led_4 (.in(\controller_1_节拍1 ));
  Register \u_寄存器_D  (.D(ram_1_data), .en(\controller_1_使能d寄存器 ), .Q(\寄存器_D_q ), .clk(CLK), .clr(RST));
  LED led_5 (.in(\controller_1_节拍5 ));
  LED led_6 (.in(\controller_1_节拍4 ));
  // Probe on controller_1_ir
  // Probe on controller_1_pc
  // Probe on ram_1_data
  // Probe on \controller_1_ram地址总线 
  RAM ram_1 (.addr(\controller_1_ram地址总线 ), .data(ram_1_data), .clk(CLK), .ld(1'b1));  // open: sel, clr

  // Notes on the sheet:
  //   随机访问存储器（RAM）
  //   在简易计算机中存放指令和数据
endmodule

module Controller (
  input  \时钟 ,
  input  \复位 ,
  input  [7:0] \RAM数据总线 ,
  input  \ALU溢出 ,
  input  \ALU为负 ,
  input  \ALU为0 ,
  input  [7:0] \ALU结果 ,
  input  [7:0] \寄存器A ,
  input  [7:0] \寄存器B ,
  input  [7:0] \寄存器C ,
  input  [7:0] \寄存器D ,
  output \节拍0 ,
  output [7:0] PC,
  output \节拍1 ,
  output \节拍2 ,
  output \节拍3 ,
  output [7:0] IR,
  output \节拍4 ,
  output \节拍5 ,
  output [7:0] \RAM地址总线 ,
  output \使能A寄存器 ,
  output \使能B寄存器 ,
  output \使能C寄存器 ,
  output \使能D寄存器 ,
  output [7:0] \ALU操作数A ,
  output [7:0] \ALU操作数B ,
  output \ALU加法 ,
  output \ALU减法 
);

  wire and_1_out, and_3_out, and_7_out, and_8_out, and_9_out, and_10_out, and_11_out, and_12_out, HALT,
       IS_CALC, IS_LD, IS_STO, JMP, JNZ, JZ, LDA, LDB, LDC, LDD, not_1_out, not_2_out, not_3_out, not_4_out,
       or_4_out, or_5_out, PC_LD, RAM_A_MUX, STOA, STOB, STOC;
  wire [1:0] ALU_A_MUX, ALU_B_MUX;
  wire [7:0] bit_extender_1_out, PC_IN;
  wire [7:4] transistor_2_out;

  Loop_Counter loop_counter_1 (
    .CLK(\时钟 ), .RST(\复位 ), .T0(\节拍0 ), .T1(\节拍1 ), .T2(\节拍2 ), .T3(\节拍3 ), .T4(\节拍4 ), .T5(\节拍5 ));
  and and_1 (and_1_out, \节拍2 , IS_LD);
  Register \u_指令寄存器_IR  (.D(\RAM数据总线 ), .en(\节拍0 ), .Q(IR), .clk(\时钟 ), .clr(\复位 ));
  Counter \u_程序计数器_PC  (.load(PC_LD), .D(PC_IN), .count(\节拍1 ), .Q(PC), .clk(\时钟 ), .clr(\复位 ));  // open: carry
  // Probe on bit_extender_1_out
  assign bit_extender_1_out = {{4{1'b0}}, IR[3:0]};  // Bit_Extender bit_extender_1
  // Probe on RAM_A_MUX
  Multiplexer #(.select(2), .width(8), .enable("false")) multiplexer_1 (
    .in0(\寄存器A ), .in1(\寄存器B ), .in2(\寄存器C ), .in3(\寄存器D ), .out(\ALU操作数A ), .sel(ALU_A_MUX));
  Multiplexer #(.select(2), .width(8), .enable("false")) multiplexer_2 (
    .in0(\寄存器A ), .in1(\寄存器B ), .in2(\寄存器C ), .in3(\寄存器D ), .out(\ALU操作数B ), .sel(ALU_B_MUX));
  Multiplexer #(.width(8), .enable("false")) multiplexer_3 (
    .in0(PC), .in1(bit_extender_1_out), .out(\RAM地址总线 ), .sel(RAM_A_MUX));
  Instruction_Decoder instruction_decoder_1 (
    .IR(IR), .LDA(LDA), .LDB(LDB), .LDC(LDC), .LDD(LDD), .ADD(\ALU加法 ), .SUB(\ALU减法 ), .STOA(STOA),
    .STOB(STOB), .STOC(STOC), .STOD(STOB), .JMP(JMP), .JZ(JZ), .JNZ(JNZ), .HALT(HALT));
  and and_2 (\使能A寄存器 , LDA, \节拍3 );
  and and_3 (and_3_out, \节拍3 , IS_LD);
  and and_4 (\使能B寄存器 , LDB, \节拍3 );
  or or_1 (IS_LD, LDA, LDB, LDC, LDD);
  or or_2 (IS_CALC, \ALU加法 , \ALU减法 );
  or or_3 (IS_STO, STOA, STOB, STOC, STOB);
  and and_5 (\使能C寄存器 , LDC, \节拍3 );
  and and_6 (\使能D寄存器 , LDD, \节拍3 );
  and and_7 (and_7_out, \节拍4 , IS_LD);
  or or_4 (or_4_out, \节拍2 , \节拍3 );
  and and_8 (and_8_out, \节拍3 , IS_CALC);
  Pull_Resistor pull_resistor_1 (.node(RAM_A_MUX));
  or or_5 (or_5_out, and_7_out, and_3_out, and_1_out);
  Transistor #(.gate("br")) transistor_1 (.in(or_5_out), .out(RAM_A_MUX), .gate(\节拍0 ));
  Transistor #(.\type ("n"), .width(8)) transistor_2 (
    .in(IR), .out({transistor_2_out, ALU_A_MUX, ALU_B_MUX}), .gate(or_4_out));
  Pull_Resistor pull_resistor_2 (.node(ALU_A_MUX[0]));
  Pull_Resistor pull_resistor_3 (.node(ALU_A_MUX[1]));
  Transistor #(.\type ("n"), .width(8)) transistor_3 (.in(\ALU结果 ), .out(\RAM数据总线 ), .gate(and_8_out));
  not not_1 (not_1_out, ALU_A_MUX[0]);
  not not_2 (not_2_out, ALU_A_MUX[1]);
  not not_3 (not_3_out, ALU_A_MUX[0]);
  not not_4 (not_4_out, ALU_A_MUX[1]);
  Transistor #(.\type ("n")) transistor_4 (.in(and_9_out), .out(\使能A寄存器 ), .gate(and_8_out));
  and and_9 (and_9_out, not_1_out, not_2_out);
  Transistor #(.\type ("n")) transistor_5 (.in(and_10_out), .out(\使能B寄存器 ), .gate(and_8_out));
  and and_10 (and_10_out, not_3_out, ALU_A_MUX[1]);
  Transistor #(.\type ("n")) transistor_6 (.in(and_11_out), .out(\使能C寄存器 ), .gate(and_8_out));
  and and_11 (and_11_out, ALU_A_MUX[0], not_4_out);
  and and_12 (and_12_out, ALU_A_MUX[0], ALU_A_MUX[1]);
  Transistor #(.\type ("n")) transistor_7 (.in(and_12_out), .out(\使能D寄存器 ), .gate(and_8_out));

  // Other names for the same wires on the sheet: ADD = \ALU加法 ; ALU_A[7:0] = \ALU操作数A ; ALU_B[7:0] = \ALU操作数B ;
  //   ALU_N = \ALU为负 ; ALU_O = \ALU溢出 ; ALU_S[7:0] = \ALU结果 ; ALU_Z = \ALU为0 ; CLK = \时钟 ; RAM_A[7:0] = \RAM地址总线 ;
  //   RAM_D[7:0] = \RAM数据总线 ; REG_A[7:0] = \寄存器A ; REG_A_EN = \使能A寄存器 ; REG_B[7:0] = \寄存器B ; REG_B_EN = \使能B寄存器 ;
  //   REG_C[7:0] = \寄存器C ; REG_C_EN = \使能C寄存器 ; REG_D[7:0] = \寄存器D ; REG_D_EN = \使能D寄存器 ; RST = \复位 ; SUB = \ALU减法 ;
  //   IR_EN = \节拍0 ; T0 = \节拍0 ; PC_EN = \节拍1 ; T1 = \节拍1 ; T2 = \节拍2 ; T3 = \节拍3 ; T4 = \节拍4 ; T5 = \节拍5 

  // Notes on the sheet:
  //   当T2=1时
  //   环形计数器
  //   复用给PC，RAM@PC的指令传输给IR
  //   1. 指令为LD{A-D}时，将RAM的地址总线复用给指令的后四位
  //   当T0=1时，启用IR寄存器的写入和RAM的读取，将RAM的地址总线
  //   当T1=1时，使PC寄存器的值加一，以备读取下一条指令
  //   取指令周期
  //   执行指令周期
  //   ALU复用器组
  //   把输入端复用给不同寄存器
  //   当T3=1时
  //   1. 指令为LD{A-D}时，将RAM的地址总线复用给指令的后四位
  //   T3=1时将不同寄存器的使能端打开
  //   LDA~LDD指令逻辑
  //   当T4=1时
  //   译码部分
  //   是LOAD指令
  //   是计算指令
  //   是STO指令
  //   1. 指令为LD{A-D}时，将RAM的地址总线复用给指令的后四位
endmodule

module ALU (
  input  [7:0] \操作数A ,
  input  [7:0] \操作数B ,
  input  \加法 ,
  input  \减法 ,
  output out_5,
  output [7:0] \输出信号 ,
  output \结果为0信号 ,
  output out_8
);

  wire [7:0] adder_1_out, subtractor_1_out;

  Adder adder_1 (.a(\操作数A ), .b(\操作数B ), .out(adder_1_out), .cout(out_5));  // open: cin
  Subtractor subtractor_1 (.a(\操作数A ), .b(\操作数B ), .out(subtractor_1_out), .bout(out_8));  // open: bin
  Multiplexer #(.width(8)) multiplexer_1 (
    .in0(adder_1_out), .in1(subtractor_1_out), .out(\输出信号 ), .sel(\减法 ));  // open: en
  nor nor_1 (\结果为0信号 , \输出信号 [0], \输出信号 [1], \输出信号 [2], \输出信号 [3], \输出信号 [4], \输出信号 [5], \输出信号 [6], \输出信号 [7]);

  // Other names for the same wires on the sheet: ADD = \加法 ; SUBTRACT = \减法 
endmodule

module Instruction_Decoder (
  input  [7:0] IR,
  output LDA,
  output LDB,
  output LDC,
  output LDD,
  output ADD,
  output SUB,
  output STOA,
  output STOB,
  output STOC,
  output STOD,
  output JMP,
  output JZ,
  output JNZ,
  output HALT
);

  wire not_1_out, not_2_out, not_3_out, not_4_out, not_5_out, not_6_out, not_7_out, not_8_out, not_9_out,
       not_10_out, not_11_out, not_12_out, not_13_out, not_14_out, not_15_out, not_16_out, not_17_out,
       not_18_out, not_19_out, not_20_out, not_21_out, not_22_out, not_23_out, not_24_out, not_25_out,
       not_26_out, not_27_out, not_28_out;

  not not_1 (not_1_out, IR[7]);
  not not_2 (not_2_out, IR[6]);
  not not_3 (not_3_out, IR[5]);
  not not_4 (not_4_out, IR[7]);
  not not_5 (not_5_out, IR[6]);
  not not_6 (not_6_out, IR[4]);
  not not_7 (not_7_out, IR[7]);
  not not_8 (not_8_out, IR[6]);
  not not_9 (not_9_out, IR[7]);
  not not_10 (not_10_out, IR[5]);
  not not_11 (not_11_out, IR[4]);
  not not_12 (not_12_out, IR[7]);
  not not_13 (not_13_out, IR[5]);
  not not_14 (not_14_out, IR[7]);
  not not_15 (not_15_out, IR[4]);
  not not_16 (not_16_out, IR[7]);
  not not_17 (not_17_out, IR[6]);
  not not_18 (not_18_out, IR[5]);
  not not_19 (not_19_out, IR[4]);
  not not_20 (not_20_out, IR[6]);
  not not_21 (not_21_out, IR[5]);
  not not_22 (not_22_out, IR[6]);
  not not_23 (not_23_out, IR[4]);
  not not_24 (not_24_out, IR[6]);
  not not_25 (not_25_out, IR[5]);
  not not_26 (not_26_out, IR[4]);
  not not_27 (not_27_out, IR[5]);
  not not_28 (not_28_out, IR[4]);
  and and_1 (LDA, not_1_out, not_2_out, not_3_out, IR[4]);
  and and_2 (LDB, not_4_out, not_5_out, IR[5], not_6_out);
  and and_3 (LDC, not_7_out, not_8_out, IR[5], IR[4]);
  and and_4 (LDD, not_9_out, IR[6], not_10_out, not_11_out);
  and and_5 (ADD, not_12_out, IR[6], not_13_out, IR[4]);
  and and_6 (SUB, not_14_out, IR[6], IR[5], not_15_out);
  and and_7 (STOA, not_16_out, IR[6], IR[5], IR[4]);
  and and_8 (STOB, IR[7], not_17_out, not_18_out, not_19_out);
  and and_9 (STOC, IR[7], not_20_out, not_21_out, IR[4]);
  and and_10 (STOD, IR[7], not_22_out, IR[5], not_23_out);
  and and_11 (JMP, IR[7], not_24_out, IR[5], IR[4]);
  and and_12 (JZ, IR[7], IR[6], not_25_out, not_26_out);
  and and_13 (JNZ, IR[7], IR[6], not_27_out, IR[4]);
  and and_14 (HALT, IR[7], IR[6], IR[5], not_28_out);

  // Notes on the sheet:
  //   译码器 用途：解读从指令寄存器（IR）来的指令的头四位
endmodule

module Loop_Counter (
  input  CLK,
  input  RST,
  output T0,
  output T1,
  output T2,
  output T3,
  output T4,
  output T5
);

  D_Flip_Flop d_ff_1 (.clk(CLK), .D(T5), .Q(T0), .preset(RST));  // open: Qn, en, reset
  D_Flip_Flop d_ff_2 (.clk(CLK), .D(T0), .Q(T1), .reset(RST));  // open: Qn, preset, en
  D_Flip_Flop d_ff_3 (.clk(CLK), .D(T1), .Q(T2), .reset(RST));  // open: Qn, preset, en
  D_Flip_Flop d_ff_4 (.clk(CLK), .D(T2), .Q(T3), .reset(RST));  // open: Qn, preset, en
  D_Flip_Flop d_ff_5 (.clk(CLK), .D(T3), .Q(T4), .reset(RST));  // open: Qn, preset, en
  D_Flip_Flop d_ff_6 (.clk(CLK), .D(T4), .Q(T5), .reset(RST));  // open: Qn, preset, en

  // Notes on the sheet:
  //   复位后默认第一个D触发器为高电平
  //   环形计数器  用途：依次使T0~T6为1，让计算机在一个时钟周期里完成取指令、执行指令的操作
endmodule
